// Digital circuit 1bit-half-adder.dig as structural Verilog
module _1bit_half_adder (
  input  A,
  input  B,
  output sum
);

  wire and_1_out, and_2_out;

  and and_1 (and_1_out, ~A, B);  // And
  and and_2 (and_2_out, A, ~B);  // And
  or or_1 (sum, and_1_out, and_2_out);
endmodule
