// Digital circuit even-odd-bits.dig as structural Verilog
module even_odd_bits (
  input  n_2,
  input  n_1,
  input  n_0,
  output even,
  output odd
);

  wire and_1_out, and_2_out, and_3_out, and_4_out;

  and and_1 (and_1_out, ~n_0, ~n_1, ~n_2);  // And
  and and_2 (and_2_out, ~n_0, n_1, n_2);  // And
  and and_3 (and_3_out, n_0, ~n_1, n_2);  // And
  and and_4 (and_4_out, n_0, n_1, ~n_2);  // And
  or or_1 (even, and_1_out, and_2_out, and_3_out, and_4_out);
  not not_1 (odd, even);
endmodule
