// Digital circuit even-odd-multi.dig as structural Verilog
module even_odd_multi (
  input  [2:0] n,
  output even,
  output odd
);

  even_odd_bits even_odd_bits_1 (.n_0(n[0]), .n_1(n[1]), .n_2(n[2]), .even(even), .odd(odd));
endmodule
