// Digital circuit rom-example.dig as structural Verilog
module rom_example (
  input  [7:0] ADDR,
  output [31:0] IW,
  output [6:0] opcode,
  output [4:0] rd,
  output [6:0] itype
);

  ROM #(.AddrBits(8), .Bits(32)) Inst_Mem (.A(ADDR), .sel(1'b1), .D(IW));

  assign itype = 7'b0010011;
  assign opcode = IW[6:0];
  assign rd = IW[11:7];

  // Notes on the sheet:
  //   contents of Inst_Mem (hex, n*v repeats v):
  //   100293,a2c463,8067,fe810113,113023,a13423,fff50513,fe5ff0ef,a13823
  //   ,813503,ffe50513,fd5ff0ef,1013303,650533,13083,1810113,8067,c0001073
endmodule
