// Digital circuit inst-decode.dig as structural Verilog
module inst_decode (
  input  [31:0] IW,
  output ALUsrcB,
  output [2:0] ALUop,
  output RFW
);

  wire ADDI_2_eq, ADDI_eq, ADDR_2_eq, ADDR_3_eq, ADDR_eq, and_1_out, and_2_out, priorityencoder_1_num;

  Comparator #(.Bits(7)) ADDI (.a(IW[6:0]), .b(7'b0010011), .eq(ADDI_eq));  // open: gt, lt
  Comparator #(.Bits(3)) ADDI_2 (.a(IW[14:12]), .b(3'b000), .eq(ADDI_2_eq));  // open: gt, lt
  Comparator #(.Bits(7)) ADDR (.a(IW[6:0]), .b(7'b0010011), .eq(ADDR_eq));  // open: gt, lt
  Comparator #(.Bits(3)) ADDR_2 (.a(IW[14:12]), .b(3'b000), .eq(ADDR_2_eq));  // open: gt, lt
  Comparator #(.Bits(7)) ADDR_3 (.a(IW[31:25]), .b({7{1'b0}}), .eq(ADDR_3_eq));  // open: gt, lt
  and and_1 (and_1_out, ADDI_eq, ADDI_2_eq);
  and and_2 (and_2_out, ADDR_eq, ADDR_2_eq, ADDR_3_eq);
  PriorityEncoder priorityencoder_1 (.in0(and_1_out), .in1(and_2_out), .num(priorityencoder_1_num));  // open: any
  ROM #(.AddrBits(1), .Bits(5)) DecodeRom (.A(priorityencoder_1_num), .sel(1'b1), .D({RFW, ALUop, ALUsrcB}));

  // Other names for the same wires on the sheet: opc[6:0] = IW[6:0]; f3[2:0] = IW[14:12]; f7[6:0] = IW[31:25]

  // Notes on the sheet:
  //   contents of DecodeRom (hex, n*v repeats v):
  //   11,10
endmodule
