// Digital circuit inum-to-ascii.dig as structural Verilog
module inum_to_ascii (
  input  [1:0] inum,
  output [7:0] c0,
  output [7:0] c1,
  output [7:0] c2,
  output [7:0] c3
);

  ROM #(.Bits(32)) rom_1 (.A(inum), .sel(1'b1), .D({c0, c1, c2, c3}));

  // Notes on the sheet:
  //   contents of rom_1 (hex, n*v repeats v):
  //   41444449,41444452,4a414c5f,4a414c52
endmodule
