// Digital circuit processor.dig as structural Verilog
module processor (
  input  [1:0] inum
);

  wire [7:0] inum_to_ascii_1_c0, inum_to_ascii_1_c1, inum_to_ascii_1_c2, inum_to_ascii_1_c3;

  // Probe on inum_to_ascii_1_c0
  inum_to_ascii inum_to_ascii_1 (
    .c0(inum_to_ascii_1_c0), .c1(inum_to_ascii_1_c1), .c2(inum_to_ascii_1_c2), .c3(inum_to_ascii_1_c3),
    .inum(inum));
  // Probe on inum_to_ascii_1_c1
  // Probe on inum_to_ascii_1_c2
  // Probe on inum_to_ascii_1_c3
endmodule
